// Logisim project mips-pipeline-claura.circ as structural Verilog: 14 circuits, main circuit mips
module alu (
  input  [3:0] ALU_Control,
  input  [31:0] in_2,
  input  [31:0] in_3,
  output [31:0] out_4,
  output Zero
);

  wire comparator_1_lt;
  wire [31:0] adder_1_out, and_1_out, multiplexer_1_out, or_1_out, subtractor_1_out, xor_1_out;

  assign and_1_out = in_2 & in_3;  // AND_Gate and_1, 32 bits wide
  assign or_1_out = in_2 | in_3;  // OR_Gate or_1, 32 bits wide
  Adder #(.width(32)) adder_1 (.a(in_2), .b(in_3), .out(adder_1_out));  // open: cin, cout
  Subtractor #(.width(32)) subtractor_1 (.a(in_2), .b(in_3), .out(subtractor_1_out));  // open: bin, bout
  Comparator #(.width(32), .mode("unsigned")) comparator_1 (.a(in_2), .b(in_3), .lt(comparator_1_lt));  // open: gt, eq
  assign xor_1_out = in_2 ^ in_3;  // XOR_Gate xor_1, 32 bits wide
  Multiplexer #(.width(32), .enable("false")) multiplexer_1 (
    .in0({32{1'b0}}), .in1(32'h1), .out(multiplexer_1_out), .sel(comparator_1_lt));
  Multiplexer #(.select(4), .width(32), .disabled(0), .enable("false")) multiplexer_2 (
    .in0(and_1_out), .in1(or_1_out), .in2(adder_1_out), .in6(subtractor_1_out), .in7(multiplexer_1_out),
    .in12(xor_1_out), .out(out_4), .sel(ALU_Control));  // open: in3, in4, in5, in8, in9, in10, in11, in13, in14, in15
  Comparator #(.width(32), .mode("unsigned")) comparator_2 (.a(out_4), .b({32{1'b0}}), .eq(Zero));  // open: gt, lt

  // Notes on the sheet:
  //   A
  //   B
  //   Logic from the first table in Chapter 4.4
  //   Op selects the result
  //   Output
endmodule

module mips (
);

  wire alu_1_zero, ALUScr, beq, bne, branch_1_c, clear, clear_mem, clock, control_1_alusrc, control_1_beq,
       control_1_bne, control_1_jump, control_1_memread, control_1_memtoreg, control_1_memwrite,
       control_1_regdst, control_1_regwrite, ex_mem_1_out_16, ex_mem_1_out_18, ex_mem_1_out_19,
       id_ex_1_beq_2, id_ex_1_bne_2, id_ex_1_jump_2, id_ex_1_memread_2, id_ex_1_memtoreg_2,
       id_ex_1_memwrite_2, id_ex_1_regwrite_2, jump, load, MemtoReg, reg_pipeline, RegDst,
       Restart_Program_out, store, writereg_t, zero_cont;
  wire [1:0] ALUOp, Control, control_1_aluop, control_1_control, id_ex_1_control_2;
  wire [3:0] alu_control_1_operation;
  wire [4:0] ex_mem_1_out_26, id_ex_1_instrucao__15_11_2, id_ex_1_instrucao__20_16_2, multiplexer_1_out,
       reg_if_id_1_instruction___out_2, WriteReg;
  wire [5:0] codop, id_ex_1_immediate_2, register_1_q, register_2_q, register_3_q, register_4_q;
  wire [15:0] counter_1_q, multiplier_1_out;
  wire [25:0] reg_if_id_1_instruction___out, rom_1_data;
  wire [27:0] bit_extender_1_out, shifter_1_out;
  wire [31:0] adder_1_out, adder_2_out, alu_1_out_4, bit_extender_2_out, ex_mem_1_out_17, ex_mem_1_out_21,
       ex_mem_1_out_24, id_ex_1_data1__rs_2, id_ex_1_data2__rt_rd_2, id_ex_1_pc_4_2, load_saida,
       mem_wb_1_out_8, mem_wb_1_out_9, multiplexer_2_out, multiplexer_3_out, multiplexer_4_out, pc_4, PC_q,
       ram_1_data, reg_32_1_readdata1, rt, shifter_2_out, store_saida, write_data;
  wire [31:6] id_ex_1_immediate_2_2;
  wire [31:26] rom_1_data_2;

  Register #(.width(32)) PC (.D(multiplexer_4_out), .Q(PC_q), .clk(clock), .clr(Restart_Program_out));  // open: en
  Clock clock_1 (.out(clock));
  // Probe on adder_1_out
  Button Restart_Program (.out(Restart_Program_out));
  Button Zero_Reg_File (.out(clear));
  Button Zero_Mem_File (.out(clear_mem));
  Button Zero_Reg_Pipeline (.out(reg_pipeline));
  Button zero_contador (.out(zero_cont));
  Counter #(.width(16), .max('hffff)) counter_1 (
    .count(1'b1), .Q(counter_1_q), .clk(clock), .clr(zero_cont));  // open: load, D, carry
  Adder #(.width(32)) adder_1 (.a(PC_q), .b(32'h4), .out(adder_1_out));  // open: cin, cout
  // Probe on codop
  ROM #(.dataWidth(32)) rom_1 (.addr(PC_q[9:2]), .data({rom_1_data_2, rom_1_data}));  // open: sel
  Register #(.width(6)) register_1 (.D(codop), .Q(register_1_q), .clk(clock), .clr(reg_pipeline));  // open: en
  Multiplier #(.width(16)) multiplier_1 (.a(counter_1_q), .b(16'h64), .out(multiplier_1_out));  // open: cin, cout
  assign bit_extender_1_out = {{2{1'b0}}, rom_1_data};  // Bit_Extender bit_extender_1
  // Probe on multiplier_1_out
  Shifter #(.width(28)) shifter_1 (.in(bit_extender_1_out), .\dist (5'b00010), .out(shifter_1_out));
  Reg_IF_ID reg_if_id_1 (
    .pc_4(adder_1_out), .instruction({rom_1_data_2, rom_1_data}), .clock(clock), .pc_4___out(pc_4),
    .instruction___out({codop, reg_if_id_1_instruction___out[25:21], reg_if_id_1_instruction___out_2, reg_if_id_1_instruction___out[15:0]}),
    .clear(reg_pipeline));
  Hex_Digit_Display hex_digit_display_1 (.value(multiplier_1_out[11:8]));  // open: dp
  Hex_Digit_Display hex_digit_display_2 (.value(multiplier_1_out[15:12]));  // open: dp
  // Probe on pc_4
  // Probe on reg_if_id_1_instruction___out_2
  // Probe on reg_if_id_1_instruction___out[15:0]
  // Probe on codop
  // Probe on reg_if_id_1_instruction___out[25:21]
  // Probe on reg_if_id_1_instruction___out[15:11]
  Hex_Digit_Display hex_digit_display_3 (.value(multiplier_1_out[7:4]));  // open: dp
  Hex_Digit_Display hex_digit_display_4 (.value(multiplier_1_out[3:0]));  // open: dp
  control control_1 (
    .in_1(codop), .RegDst(control_1_regdst), .ALUSrc(control_1_alusrc), .MemtoReg(control_1_memtoreg),
    .RegWrite(control_1_regwrite), .MemRead(control_1_memread), .MemWrite(control_1_memwrite),
    .Beq(control_1_beq), .Bne(control_1_bne), .Jump(control_1_jump), .Control(control_1_control),
    .ALUOp(control_1_aluop));
  reg_32 reg_32_1 (
    .ReadReg1(reg_if_id_1_instruction___out[25:21]), .ReadReg2(reg_if_id_1_instruction___out_2),
    .WriteReg(WriteReg), .RegWrite(writereg_t), .ReadData1(reg_32_1_readdata1), .ReadData2(rt),
    .WriteData(write_data), .Clk(clock), .Reset(clear));
  // Probe on reg_if_id_1_instruction___out[25:21]
  // Probe on reg_if_id_1_instruction___out_2
  // Probe on WriteReg
  // Probe on register_1_q
  Register #(.width(6)) register_2 (.D(register_1_q), .Q(register_2_q), .clk(clock), .clr(reg_pipeline));  // open: en
  // Probe on reg_if_id_1_instruction___out_2
  assign bit_extender_2_out = {{16{reg_if_id_1_instruction___out[15]}}, reg_if_id_1_instruction___out[15:0]};  // Bit_Extender bit_extender_2
  ID_EX id_ex_1 (
    .data1__rs(reg_32_1_readdata1), .data2__rt_rd(rt), .immediate(bit_extender_2_out),
    .instrucao__20_16(reg_if_id_1_instruction___out_2),
    .instrucao__15_11(reg_if_id_1_instruction___out[15:11]), .clock(clock),
    .data1__rs_2(id_ex_1_data1__rs_2), .data2__rt_rd_2(id_ex_1_data2__rt_rd_2),
    .immediate_2({id_ex_1_immediate_2_2, id_ex_1_immediate_2}),
    .instrucao__20_16_2(id_ex_1_instrucao__20_16_2), .instrucao__15_11_2(id_ex_1_instrucao__15_11_2),
    .clear(reg_pipeline), .pc_4(pc_4), .pc_4_2(id_ex_1_pc_4_2), .RegDst_2(RegDst), .ALUSrc_2(ALUScr),
    .MemtoReg_2(id_ex_1_memtoreg_2), .RegWrite_2(id_ex_1_regwrite_2), .MemRead_2(id_ex_1_memread_2),
    .MemWrite_2(id_ex_1_memwrite_2), .Beq_2(id_ex_1_beq_2), .Bne_2(id_ex_1_bne_2), .Jump_2(id_ex_1_jump_2),
    .Control_2(id_ex_1_control_2), .ALUOp_2(ALUOp), .RegDst(control_1_regdst), .ALUSrc(control_1_alusrc),
    .MemtoReg(control_1_memtoreg), .RegWrite(control_1_regwrite), .MemRead(control_1_memread),
    .MemWrite(control_1_memwrite), .Beq(control_1_beq), .Bne(control_1_bne), .Jump(control_1_jump),
    .Control(control_1_control), .ALUOp(control_1_aluop));
  // Probe on reg_if_id_1_instruction___out[15:11]
  // Probe on id_ex_1_instrucao__15_11_2
  Multiplexer #(.width(5), .enable("false")) multiplexer_1 (
    .in0(id_ex_1_instrucao__20_16_2), .in1(id_ex_1_instrucao__15_11_2), .out(multiplexer_1_out), .sel(RegDst));
  // Probe on id_ex_1_data1__rs_2
  // Probe on id_ex_1_data2__rt_rd_2
  // Probe on multiplexer_1_out
  Shifter #(.width(32)) shifter_2 (
    .in({id_ex_1_immediate_2_2, id_ex_1_immediate_2}), .\dist (5'b00010), .out(shifter_2_out));
  Multiplexer #(.width(32), .enable("false")) multiplexer_2 (
    .in0(id_ex_1_data2__rt_rd_2), .in1({id_ex_1_immediate_2_2, id_ex_1_immediate_2}),
    .out(multiplexer_2_out), .sel(ALUScr));
  // Probe on multiplexer_2_out
  alu_control alu_control_1 (.Operation(alu_control_1_operation), .ALUOp(ALUOp), .Function(id_ex_1_immediate_2));
  Adder #(.width(32)) adder_2 (.a(id_ex_1_pc_4_2), .b(shifter_2_out), .out(adder_2_out));  // open: cin, cout
  alu alu_1 (
    .out_4(alu_1_out_4), .Zero(alu_1_zero), .in_2(id_ex_1_data1__rs_2), .in_3(multiplexer_2_out),
    .ALU_Control(alu_control_1_operation));
  // Probe on alu_control_1_operation
  // Probe on register_2_q
  Register #(.width(6)) register_3 (.D(register_2_q), .Q(register_3_q), .clk(clock), .clr(reg_pipeline));  // open: en
  // Probe on alu_1_out_4
  EX_MEM ex_mem_1 (
    .pc_deslocado(adder_2_out), .zero(alu_1_zero), .AluResult(alu_1_out_4), .rt(id_ex_1_data2__rt_rd_2),
    .WriteReg_2(multiplexer_1_out), .clock(clock), .out_17(ex_mem_1_out_17), .out_19(ex_mem_1_out_19),
    .out_24(ex_mem_1_out_24), .out_26(ex_mem_1_out_26), .MemToReg(id_ex_1_memtoreg_2),
    .WriteReg(id_ex_1_regwrite_2), .Load(id_ex_1_memread_2), .store(id_ex_1_memwrite_2), .beq(id_ex_1_beq_2),
    .bne(id_ex_1_bne_2), .jump(id_ex_1_jump_2), .control(id_ex_1_control_2), .out_16(ex_mem_1_out_16),
    .out_18(ex_mem_1_out_18), .out_20(load), .out_22(store), .out_23(beq), .out_25(bne), .out_27(jump),
    .out_28(Control), .clear(reg_pipeline), .out_21(ex_mem_1_out_21));
  // Probe on ex_mem_1_out_26
  // Probe on multiplexer_4_out
  // Probe on adder_1_out
  Multiplexer #(.width(32), .enable("false")) multiplexer_3 (
    .in0(adder_1_out), .in1(ex_mem_1_out_17), .out(multiplexer_3_out), .sel(branch_1_c));
  load_store u_store (.Entrada(ex_mem_1_out_24), .Saida(store_saida), .Control(Control));
  Multiplexer #(.width(32), .enable("false")) multiplexer_4 (
    .in0(multiplexer_3_out), .in1({adder_1_out[31:28], shifter_1_out}), .out(multiplexer_4_out), .sel(jump));
  branch branch_1 (.beq(beq), .bne(bne), .ZERO(ex_mem_1_out_19), .C(branch_1_c));
  // Probe on ex_mem_1_out_21
  // Probe on store_saida
  // Probe on ex_mem_1_out_21[9:2]
  // Probe on register_3_q
  Register #(.width(6)) register_4 (.D(register_3_q), .Q(register_4_q), .clk(clock), .clr(reg_pipeline));  // open: en
  RAM #(.dataWidth(32), .bus("separate")) ram_1 (
    .addr(ex_mem_1_out_21[9:2]), .din(store_saida), .data(ram_1_data), .str(store), .clk(clock), .ld(load),
    .clr(clear_mem));  // open: sel
  MEM_WB mem_wb_1 (
    .MemToReg(ex_mem_1_out_16), .WriteReg(ex_mem_1_out_18), .RegWrite(ex_mem_1_out_26), .out_10(MemtoReg),
    .out_11(writereg_t), .out_12(WriteReg), .clock(clock), .clear(reg_pipeline), .pc_deslocado(ram_1_data),
    .out_8(mem_wb_1_out_8), .AluResult(ex_mem_1_out_21), .out_9(mem_wb_1_out_9));
  // Probe on WriteReg
  load_store u_load (.Entrada(mem_wb_1_out_8), .Saida(load_saida), .Control(Control));
  // Probe on load_saida
  // Probe on mem_wb_1_out_9
  // Probe on register_4_q
  Multiplexer #(.width(32), .enable("false")) multiplexer_5 (
    .in0(mem_wb_1_out_9), .in1(load_saida), .out(write_data), .sel(MemtoReg));
  Register #(.width(6)) register_5 (.D(register_4_q), .clk(clock), .clr(reg_pipeline));  // open: en, Q
  // Probe on write_data

  // Notes on the sheet:
  //   CLARA LETÍCIA LOPES DE OLIVEIRA / MARIA LAURA BARBOZA MORONI
  //   Clock
  //   Next PC
  //   Memória de instrução
  //   IF
  //   contents of rom_1 (hex, n*v repeats v):
  //   8c090000 8c0a0004 211402a 211402a 211402a 12a5820 211402a 211402a 211402a ac0b000c
  //   rt
  //   immediate
  //   Reg Write Data
  //   rs
  //   ID
  //   rt
  //   rs
  //   EX
  //   ALU Op
  //   MemToReg
  //   WriteReg
  //   Mem Addr
  //   MEM
  //   Memória de dados
  //   WB
  //   Saída
endmodule

module instruction_type_decode (
  input  [5:0] _5_4_3_2_1_0,
  output R_format,
  output j,
  output beq,
  output bne,
  output addi,
  output slti,
  output andi,
  output ori,
  output lb,
  output lh,
  output lw,
  output sb,
  output sh,
  output sw
);

  wire comparator_1_lt, demultiplexer_1_out0, demultiplexer_1_out1, demultiplexer_1_out4,
       demultiplexer_1_out5;

  Comparator #(.width(6), .mode("unsigned")) comparator_1 (
    .a({6{1'b0}}), .b(_5_4_3_2_1_0), .eq(R_format), .lt(comparator_1_lt));  // open: gt
  Demultiplexer #(.select(3), .enable("false")) demultiplexer_1 (
    .out0(demultiplexer_1_out0), .out1(demultiplexer_1_out1), .out4(demultiplexer_1_out4),
    .out5(demultiplexer_1_out5), .in(comparator_1_lt), .sel(_5_4_3_2_1_0[5:3]));  // open: out2, out3, out6, out7
  Demultiplexer #(.select(2), .enable("false")) demultiplexer_2 (
    .out0(lb), .out1(lh), .out3(lw), .in(demultiplexer_1_out4), .sel(_5_4_3_2_1_0[1:0]));  // open: out2
  Demultiplexer #(.select(2), .enable("false")) demultiplexer_3 (
    .out0(sb), .out1(sh), .out3(sw), .in(demultiplexer_1_out5), .sel(_5_4_3_2_1_0[1:0]));  // open: out2
  Demultiplexer #(.select(3), .enable("false")) demultiplexer_4 (
    .out0(addi), .out2(slti), .out4(andi), .out5(ori), .in(demultiplexer_1_out1), .sel(_5_4_3_2_1_0[2:0]));  // open: out1, out3, out6, out7
  Demultiplexer #(.select(3), .enable("false")) demultiplexer_5 (
    .out2(j), .out4(beq), .out5(bne), .in(demultiplexer_1_out0), .sel(_5_4_3_2_1_0[2:0]));  // open: out0, out1, out3, out6, out7

  // Other names for the same wires on the sheet: desvio[2:0] = _5_4_3_2_1_0[2:0]; memoria[1:0] = _5_4_3_2_1_0[1:0];
  //   r_imediato[2:0] = _5_4_3_2_1_0[2:0]; tipo[2:0] = _5_4_3_2_1_0[5:3]

  // Notes on the sheet:
  //   opcode
  //   This example sets "R-format" to true if opcode=00.
  //   ToDo: Fill in the logic from Fig 4.22 to determine the instruction type
  //   Hint: Use comparators and a constant to check for the right values
  //   001 - r imediatos
  //   100 - load
  //   101 - store
  //   000 - desvio
endmodule

module control_decode (
  input  Rformat,
  input  beq,
  input  bne,
  input  addi,
  input  slti,
  input  andi,
  input  ori,
  input  lb,
  input  lh,
  input  lw,
  input  sb,
  input  sh,
  input  sw,
  input  j,
  output RegDst,
  output ALUSrc,
  output MemtoReg,
  output RegWrite,
  output MemRead,
  output MemWrite,
  output Beq_2,
  output Bne_2,
  output Jump,
  output [1:0] Control,
  output ALUOp1,
  output ALUOp0
);

  wire [2:0] comparator_1_gt;
  wire [12:0] multiplexer_1_out, multiplexer_2_out, multiplexer_3_out;

  // Probe on {slti, addi, bne, beq, Rformat}
  Comparator #(.width(5), .mode("unsigned")) comparator_1 (
    .a({slti, addi, bne, beq, Rformat}), .b({5{1'b0}}), .gt(comparator_1_gt[0]));  // open: eq, lt
  Comparator #(.width(5), .mode("unsigned")) comparator_2 (
    .a({lw, lh, lb, ori, andi}), .b({5{1'b0}}), .gt(comparator_1_gt[1]));  // open: eq, lt
  // Probe on comparator_1_gt
  Comparator #(.width(4), .mode("unsigned")) comparator_3 (
    .a({j, sw, sh, sb}), .b(4'b0000), .gt(comparator_1_gt[2]));  // open: eq, lt
  Multiplexer #(.select(4), .width(13), .enable("false")) multiplexer_1 (
    .in1(13'h22), .in2(13'h422), .in4(13'h222), .in8(13'h100), .out(multiplexer_1_out), .sel({j, sw, sh, sb}));  // open: in0, in3, in5, in6, in7, in9, in10, in11, in12, in13, in14, in15
  Multiplexer #(.select(5), .width(13), .enable("false")) multiplexer_2 (
    .in1(13'h809), .in2(13'h1040), .in4(13'h1080), .in8(13'ha), .in16(13'h1008), .out(multiplexer_2_out),
    .sel({slti, addi, bne, beq, Rformat}));  // open: in0, in3, in5, in6, in7, in9, in10, in11, in12, in13, in14, in15, in17, in18, in19, in20, in21, in22, in23, in24, in25, in26, in27, in28, in29, in30, in31
  Multiplexer #(.select(5), .width(13), .enable("false")) multiplexer_3 (
    .in1(13'h808), .in2(13'h1808), .in4(13'h1e), .in8(13'h41e), .in16(13'h21e), .out(multiplexer_3_out),
    .sel({lw, lh, lb, ori, andi}));  // open: in0, in3, in5, in6, in7, in9, in10, in11, in12, in13, in14, in15, in17, in18, in19, in20, in21, in22, in23, in24, in25, in26, in27, in28, in29, in30, in31
  // Probe on {ALUOp0, ALUOp1, Control, Jump, Bne_2, Beq_2, MemWrite, MemRead, RegWrite, MemtoReg, ALUSrc, RegDst}
  Multiplexer #(.select(3), .width(13), .enable("false")) multiplexer_4 (
    .in1(multiplexer_2_out), .in2(multiplexer_3_out), .in4(multiplexer_1_out),
    .out({ALUOp0, ALUOp1, Control, Jump, Bne_2, Beq_2, MemWrite, MemRead, RegWrite, MemtoReg, ALUSrc, RegDst}),
    .sel(comparator_1_gt));  // open: in0, in3, in5, in6, in7

  // Notes on the sheet:
  //   a ordem ta invertida
  //   lb - 0 1 1 1 1 0 0 0 0 0 0 0 0
  //   lh - 0 1 1 1 1 0 0 0 0 0 1 0 0
  //   lw - 0 1 1 1 1 0 0 0 0 1 0 0 0
  //   sb - 0 1 0 0 0 1 0 0 0 0 0 0 0
  //   sh - 0 1 0 0 0 1 0 0 0 0 1 0 0
  //   sw - 0 1 0 0 0 1 0 0 0 1 0 0 0
  //   beq - 0 0 0 0 0 0 1 0 0 0 0 0 1
  //   bne - 0 0 0 0 0 0 0 1 0 0 0 0 1
  //   addi - 0 1 0 1 0 0 0 0 0 0 0 0 0
  //   slti - 0 0 0 1 0 0 0 0 0 0 0 0 1
  //   andi - 0 0 0 1 0 0 0 0 0 0 0 1 0
  //   ori - 0 0 0 1 0 0 0 0 0 0 0 1 1
  //   12 11 10 9 8 7 6 5 4 3 2 1 0
  //   r - 1 0 0 1 0 0 0 0 0 0 0 1 0
  //   j - 0 0 0 0 0 0 0 0 1 0 0 0 0 
  //   -> vai depender do funct
endmodule

module alu_control (
  input  [5:0] Function,
  input  [1:0] ALUOp,
  output [3:0] Operation
);

  wire and_1_out, and_2_out, and_3_out, and_4_out, and_5_out, and_6_out, and_7_out, and_8_out, and_9_out,
       and_10_out, not_1_out, not_2_out, not_3_out, not_4_out, not_5_out, not_6_out, not_7_out, not_8_out,
       not_9_out, not_10_out, not_11_out, not_12_out, not_13_out, not_14_out, not_15_out, not_16_out,
       not_17_out, not_18_out, not_19_out, not_20_out, not_21_out, not_22_out, not_23_out, not_24_out,
       not_25_out, not_26_out, not_27_out, or_1_out, or_2_out, or_3_out, or_4_out, or_5_out;
  wire [2:0] priority_encoder_1_out;

  not not_1 (not_1_out, ALUOp[1]);
  not not_2 (not_2_out, ALUOp[0]);
  not not_3 (not_3_out, ALUOp[0]);
  not not_4 (not_4_out, Function[3]);
  not not_5 (not_5_out, Function[2]);
  not not_6 (not_6_out, Function[1]);
  not not_7 (not_7_out, Function[0]);
  not not_8 (not_8_out, ALUOp[1]);
  not not_9 (not_9_out, ALUOp[0]);
  not not_10 (not_10_out, Function[3]);
  not not_11 (not_11_out, Function[2]);
  not not_12 (not_12_out, Function[0]);
  not not_13 (not_13_out, ALUOp[0]);
  not not_14 (not_14_out, Function[4]);
  not not_15 (not_15_out, Function[3]);
  not not_16 (not_16_out, Function[1]);
  not not_17 (not_17_out, Function[0]);
  not not_18 (not_18_out, ALUOp[0]);
  not not_19 (not_19_out, Function[4]);
  not not_20 (not_20_out, Function[3]);
  not not_21 (not_21_out, Function[1]);
  not not_22 (not_22_out, ALUOp[1]);
  not not_23 (not_23_out, ALUOp[0]);
  not not_24 (not_24_out, Function[4]);
  not not_25 (not_25_out, Function[2]);
  not not_26 (not_26_out, Function[0]);
  and and_1 (and_1_out, not_1_out, not_2_out);
  and and_2 (and_2_out, ALUOp[1], not_3_out, not_4_out, not_5_out, not_6_out, not_7_out);
  and and_3 (and_3_out, not_8_out, ALUOp[0]);
  and and_4 (and_4_out, ALUOp[1], not_9_out, not_10_out, not_11_out, Function[1], not_12_out);
  and and_5 (and_5_out, ALUOp[1], not_27_out);
  not not_27 (not_27_out, ALUOp[0]);
  and and_6 (and_6_out, ALUOp[1], not_13_out, Function[5], not_14_out, not_15_out, Function[2], not_16_out, not_17_out);
  and and_7 (and_7_out, ALUOp[1], ALUOp[0]);
  and and_8 (and_8_out, ALUOp[1], not_18_out, Function[5], not_19_out, not_20_out, Function[2], not_21_out, Function[0]);
  and and_9 (and_9_out, not_22_out, ALUOp[0]);
  and and_10 (and_10_out, ALUOp[1], not_23_out, Function[5], not_24_out, Function[3], not_25_out, Function[1], not_26_out);
  or or_1 (or_1_out, and_1_out, and_2_out);
  or or_2 (or_2_out, and_3_out, and_4_out);
  or or_3 (or_3_out, and_5_out, and_6_out);
  or or_4 (or_4_out, and_7_out, and_8_out);
  buf or_5 (or_5_out, and_10_out);  // OR_Gate
  Priority_Encoder priority_encoder_1 (
    .in0(or_3_out), .in1(or_4_out), .in2(or_1_out), .in3(or_2_out), .in4(or_5_out),
    .out(priority_encoder_1_out));  // open: in5, in6, in7, en_in, gs, en_out
  Multiplexer #(.select(3), .width(4)) multiplexer_1 (
    .in0(4'b0000), .in1(4'b0001), .in2(4'b0010), .in3(4'b0110), .in4(4'b0111), .out(Operation),
    .sel(priority_encoder_1_out));  // open: in5, in6, in7, en
  // Probe on priority_encoder_1_out

  // Notes on the sheet:
  //   Inputs
  //   B -- OR
  //   A
  //   ToDo: Fill in logic from Fig 4.13
  //   Hint: Here is the logic for the first row: 
  //   A -- if (ALUOp1=0 and ALUOp0=0)
  //   D -- then output = 2 = 0010
  //   A
  //   C
  //   A
  //   C
  //   A
  //   A
  //   C -- if (ALUOp1=1 and ALUOp0=0 and F3, F2, F1, F0 are all 0)
  //   B
  //   B
  //   B
  //   B
  //   B
  //   True for 0010=2
  //   True for 0110=6
  //   True for 0001=1
  //   True for 0111=7
  //   True for 0000=0
  //   ALUOp
  //   00
  //   01
  //   10
  //   11
  //   We have 5 possible outputs
  //   D
  //   LIVRO - PÁGINA 439
  //   Operation
  //   0010
  //   0110
  //   0010
  //   xxxx
  //   Depending on which input is 1,
  //   one of the outputs above will be selected.
  //   00 - xxxxx - 0010
  //   01 - xxxxx - 0110
  //   10 - 100000 - 0010
  //   10 - 100010 - 0110
  //   10 - 100100 - 0000
  //   10 - 100101 - 0001
  //   10 - 101010 - 0010
endmodule

module control (
  input  [5:0] in_1,
  output RegDst,
  output ALUSrc,
  output MemtoReg,
  output RegWrite,
  output MemRead,
  output MemWrite,
  output Beq,
  output Bne,
  output Jump,
  output [1:0] Control,
  output [1:0] ALUOp
);

  wire instruction_type_decode_1_addi, instruction_type_decode_1_andi, instruction_type_decode_1_beq,
       instruction_type_decode_1_bne, instruction_type_decode_1_j, instruction_type_decode_1_lb,
       instruction_type_decode_1_lh, instruction_type_decode_1_lw, instruction_type_decode_1_ori,
       instruction_type_decode_1_r_format, instruction_type_decode_1_sb, instruction_type_decode_1_sh,
       instruction_type_decode_1_slti, instruction_type_decode_1_sw;

  instruction_type_decode instruction_type_decode_1 (
    ._5_4_3_2_1_0(in_1), .R_format(instruction_type_decode_1_r_format), .beq(instruction_type_decode_1_beq),
    .bne(instruction_type_decode_1_bne), .addi(instruction_type_decode_1_addi),
    .slti(instruction_type_decode_1_slti), .andi(instruction_type_decode_1_andi),
    .ori(instruction_type_decode_1_ori), .lb(instruction_type_decode_1_lb),
    .lh(instruction_type_decode_1_lh), .lw(instruction_type_decode_1_lw), .sb(instruction_type_decode_1_sb),
    .sh(instruction_type_decode_1_sh), .sw(instruction_type_decode_1_sw), .j(instruction_type_decode_1_j));
  control_decode control_decode_1 (
    .Rformat(instruction_type_decode_1_r_format), .RegDst(RegDst), .beq(instruction_type_decode_1_beq),
    .ALUSrc(ALUSrc), .bne(instruction_type_decode_1_bne), .addi(instruction_type_decode_1_addi),
    .MemtoReg(MemtoReg), .slti(instruction_type_decode_1_slti), .RegWrite(RegWrite), .MemRead(MemRead),
    .MemWrite(MemWrite), .Beq_2(Beq), .andi(instruction_type_decode_1_andi), .Bne_2(Bne),
    .ori(instruction_type_decode_1_ori), .Jump(Jump), .lb(instruction_type_decode_1_lb), .Control(Control),
    .lh(instruction_type_decode_1_lh), .ALUOp1(ALUOp[1]), .lw(instruction_type_decode_1_lw),
    .ALUOp0(ALUOp[0]), .sb(instruction_type_decode_1_sb), .sh(instruction_type_decode_1_sh),
    .sw(instruction_type_decode_1_sw), .j(instruction_type_decode_1_j));

  // Notes on the sheet:
  //   Instruction OpCode
  //   Decode the Instruction Type first
  //   From the Insturction Type,
  //   decode the control signals
endmodule

module reg_32 (
  input  [4:0] ReadReg1,
  input  [4:0] ReadReg2,
  input  [4:0] WriteReg,
  input  RegWrite,
  input  [31:0] WriteData,
  input  Clk,
  input  Reset,
  output [31:0] ReadData1,
  output [31:0] ReadData2
);

  wire decoder_1_out0, decoder_1_out1, decoder_2_out0, decoder_2_out1, decoder_2_out2, decoder_2_out3,
       decoder_3_out0, decoder_3_out1, decoder_3_out2, decoder_3_out3, decoder_4_out0, decoder_4_out1,
       decoder_4_out2, decoder_4_out3, decoder_5_out0, decoder_5_out1, decoder_5_out2, decoder_5_out3,
       decoder_6_out0, decoder_6_out1, decoder_6_out2, decoder_6_out3, decoder_7_out0, decoder_7_out1,
       decoder_7_out2, decoder_7_out3, decoder_8_out0, decoder_8_out1, decoder_8_out2, decoder_8_out3,
       decoder_9_out0, decoder_9_out1, decoder_9_out2, decoder_9_out3, decoder_10_out0, decoder_10_out1,
       decoder_10_out2, decoder_10_out3, decoder_11_out0, decoder_11_out1, decoder_11_out2, decoder_11_out3;
  wire [31:0] multiplexer_1_out, multiplexer_2_out, multiplexer_3_out, multiplexer_4_out, multiplexer_5_out,
       multiplexer_6_out, multiplexer_7_out, multiplexer_8_out, multiplexer_9_out, multiplexer_10_out,
       multiplexer_13_out, multiplexer_14_out, multiplexer_15_out, multiplexer_16_out, multiplexer_17_out,
       multiplexer_18_out, multiplexer_19_out, multiplexer_20_out, multiplexer_21_out, multiplexer_22_out,
       register_1_q, register_2_q, register_3_q, register_4_q, register_5_q, register_6_q, register_7_q,
       register_8_q, register_9_q, register_10_q, register_11_q, register_12_q, register_13_q, register_14_q,
       register_15_q, register_16_q, register_17_q, register_18_q, register_19_q, register_20_q,
       register_21_q, register_22_q, register_23_q, register_24_q, register_25_q, register_26_q,
       register_27_q, register_28_q, register_29_q, register_30_q, register_31_q;

  // Probe on WriteReg
  Decoder #(.disabled(0)) decoder_1 (.out0(decoder_1_out0), .out1(decoder_1_out1), .sel(WriteReg[4]), .en(RegWrite));
  Decoder #(.select(2), .disabled(0)) decoder_2 (
    .out0(decoder_2_out0), .out1(decoder_2_out1), .out2(decoder_2_out2), .out3(decoder_2_out3),
    .sel(WriteReg[3:2]), .en(decoder_1_out0));
  Decoder #(.select(2), .disabled(0)) decoder_3 (
    .out0(decoder_3_out0), .out1(decoder_3_out1), .out2(decoder_3_out2), .out3(decoder_3_out3),
    .sel(WriteReg[1:0]), .en(decoder_2_out0));
  Decoder #(.select(2), .disabled(0)) decoder_4 (
    .out0(decoder_4_out0), .out1(decoder_4_out1), .out2(decoder_4_out2), .out3(decoder_4_out3),
    .sel(WriteReg[1:0]), .en(decoder_2_out1));
  Decoder #(.select(2), .disabled(0)) decoder_5 (
    .out0(decoder_5_out0), .out1(decoder_5_out1), .out2(decoder_5_out2), .out3(decoder_5_out3),
    .sel(WriteReg[1:0]), .en(decoder_2_out2));
  Decoder #(.select(2), .disabled(0)) decoder_6 (
    .out0(decoder_6_out0), .out1(decoder_6_out1), .out2(decoder_6_out2), .out3(decoder_6_out3),
    .sel(WriteReg[1:0]), .en(decoder_2_out3));
  Register #(.width(32)) register_1 (.D(WriteData), .en(decoder_3_out1), .Q(register_1_q), .clk(Clk), .clr(Reset));
  Register #(.width(32)) register_2 (.D(WriteData), .en(decoder_3_out2), .Q(register_2_q), .clk(Clk), .clr(Reset));
  Register #(.width(32)) register_3 (.D(WriteData), .en(decoder_3_out3), .Q(register_3_q), .clk(Clk), .clr(Reset));
  Register #(.width(32)) register_4 (.D(WriteData), .en(decoder_4_out0), .Q(register_4_q), .clk(Clk), .clr(Reset));
  Register #(.width(32)) register_5 (.D(WriteData), .en(decoder_4_out1), .Q(register_5_q), .clk(Clk), .clr(Reset));
  Register #(.width(32)) register_6 (.D(WriteData), .en(decoder_4_out2), .Q(register_6_q), .clk(Clk), .clr(Reset));
  Register #(.width(32)) register_7 (.D(WriteData), .en(decoder_4_out3), .Q(register_7_q), .clk(Clk), .clr(Reset));
  Register #(.width(32)) register_8 (.D(WriteData), .en(decoder_5_out0), .Q(register_8_q), .clk(Clk), .clr(Reset));
  Register #(.width(32)) register_9 (.D(WriteData), .en(decoder_5_out1), .Q(register_9_q), .clk(Clk), .clr(Reset));
  Register #(.width(32)) register_10 (.D(WriteData), .en(decoder_5_out2), .Q(register_10_q), .clk(Clk), .clr(Reset));
  Register #(.width(32)) register_11 (.D(WriteData), .en(decoder_5_out3), .Q(register_11_q), .clk(Clk), .clr(Reset));
  Register #(.width(32)) register_12 (.D(WriteData), .en(decoder_6_out0), .Q(register_12_q), .clk(Clk), .clr(Reset));
  Register #(.width(32)) register_13 (.D(WriteData), .en(decoder_6_out1), .Q(register_13_q), .clk(Clk), .clr(Reset));
  Register #(.width(32)) register_14 (.D(WriteData), .en(decoder_6_out2), .Q(register_14_q), .clk(Clk), .clr(Reset));
  Register #(.width(32)) register_15 (.D(WriteData), .en(decoder_6_out3), .Q(register_15_q), .clk(Clk), .clr(Reset));
  // Probe on {32{1'b0}}
  // Probe on register_1_q
  // Probe on register_2_q
  // Probe on register_3_q
  // Probe on register_4_q
  // Probe on register_5_q
  // Probe on register_6_q
  // Probe on register_7_q
  // Probe on register_8_q
  // Probe on register_9_q
  // Probe on register_10_q
  // Probe on register_11_q
  // Probe on register_12_q
  // Probe on register_13_q
  // Probe on register_14_q
  // Probe on register_15_q
  // Probe on ReadReg1
  Multiplexer #(.select(2), .width(32), .enable("false")) multiplexer_1 (
    .in0({32{1'b0}}), .in1(register_1_q), .in2(register_2_q), .in3(register_3_q), .out(multiplexer_1_out),
    .sel(ReadReg1[1:0]));
  Multiplexer #(.select(2), .width(32), .enable("false")) multiplexer_2 (
    .in0(register_4_q), .in1(register_5_q), .in2(register_6_q), .in3(register_7_q), .out(multiplexer_2_out),
    .sel(ReadReg1[1:0]));
  Multiplexer #(.select(2), .width(32), .enable("false")) multiplexer_3 (
    .in0(register_8_q), .in1(register_9_q), .in2(register_10_q), .in3(register_11_q),
    .out(multiplexer_3_out), .sel(ReadReg1[1:0]));
  Multiplexer #(.select(2), .width(32), .enable("false")) multiplexer_4 (
    .in0(register_12_q), .in1(register_13_q), .in2(register_14_q), .in3(register_15_q),
    .out(multiplexer_4_out), .sel(ReadReg1[1:0]));
  // Probe on ReadReg2
  Multiplexer #(.select(2), .width(32), .enable("false")) multiplexer_5 (
    .in0({32{1'b0}}), .in1(register_1_q), .in2(register_2_q), .in3(register_3_q), .out(multiplexer_5_out),
    .sel(ReadReg2[1:0]));
  Multiplexer #(.select(2), .width(32), .enable("false")) multiplexer_6 (
    .in0(register_4_q), .in1(register_5_q), .in2(register_6_q), .in3(register_7_q), .out(multiplexer_6_out),
    .sel(ReadReg2[1:0]));
  Multiplexer #(.select(2), .width(32), .enable("false")) multiplexer_7 (
    .in0(register_8_q), .in1(register_9_q), .in2(register_10_q), .in3(register_11_q),
    .out(multiplexer_7_out), .sel(ReadReg2[1:0]));
  Multiplexer #(.select(2), .width(32), .enable("false")) multiplexer_8 (
    .in0(register_12_q), .in1(register_13_q), .in2(register_14_q), .in3(register_15_q),
    .out(multiplexer_8_out), .sel(ReadReg2[1:0]));
  Multiplexer #(.select(2), .width(32), .enable("false")) multiplexer_9 (
    .in0(multiplexer_5_out), .in1(multiplexer_6_out), .in2(multiplexer_7_out), .in3(multiplexer_8_out),
    .out(multiplexer_9_out), .sel(ReadReg2[3:2]));
  Multiplexer #(.select(2), .width(32), .enable("false")) multiplexer_10 (
    .in0(multiplexer_1_out), .in1(multiplexer_2_out), .in2(multiplexer_3_out), .in3(multiplexer_4_out),
    .out(multiplexer_10_out), .sel(ReadReg1[3:2]));
  Decoder #(.select(2), .disabled(0)) decoder_7 (
    .out0(decoder_7_out0), .out1(decoder_7_out1), .out2(decoder_7_out2), .out3(decoder_7_out3),
    .sel(WriteReg[3:2]), .en(decoder_1_out1));
  Decoder #(.select(2), .disabled(0)) decoder_8 (
    .out0(decoder_8_out0), .out1(decoder_8_out1), .out2(decoder_8_out2), .out3(decoder_8_out3),
    .sel(WriteReg[1:0]), .en(decoder_7_out0));
  Decoder #(.select(2), .disabled(0)) decoder_9 (
    .out0(decoder_9_out0), .out1(decoder_9_out1), .out2(decoder_9_out2), .out3(decoder_9_out3),
    .sel(WriteReg[1:0]), .en(decoder_7_out1));
  Decoder #(.select(2), .disabled(0)) decoder_10 (
    .out0(decoder_10_out0), .out1(decoder_10_out1), .out2(decoder_10_out2), .out3(decoder_10_out3),
    .sel(WriteReg[1:0]), .en(decoder_7_out2));
  Decoder #(.select(2), .disabled(0)) decoder_11 (
    .out0(decoder_11_out0), .out1(decoder_11_out1), .out2(decoder_11_out2), .out3(decoder_11_out3),
    .sel(WriteReg[1:0]), .en(decoder_7_out3));
  Register #(.width(32)) register_16 (.D(WriteData), .en(decoder_8_out0), .Q(register_16_q), .clk(Clk), .clr(Reset));
  Register #(.width(32)) register_17 (.D(WriteData), .en(decoder_8_out1), .Q(register_17_q), .clk(Clk), .clr(Reset));
  Register #(.width(32)) register_18 (.D(WriteData), .en(decoder_8_out2), .Q(register_18_q), .clk(Clk), .clr(Reset));
  Register #(.width(32)) register_19 (.D(WriteData), .en(decoder_8_out3), .Q(register_19_q), .clk(Clk), .clr(Reset));
  Register #(.width(32)) register_20 (.D(WriteData), .en(decoder_9_out0), .Q(register_20_q), .clk(Clk), .clr(Reset));
  Register #(.width(32)) register_21 (.D(WriteData), .en(decoder_9_out1), .Q(register_21_q), .clk(Clk), .clr(Reset));
  Register #(.width(32)) register_22 (.D(WriteData), .en(decoder_9_out2), .Q(register_22_q), .clk(Clk), .clr(Reset));
  Register #(.width(32)) register_23 (.D(WriteData), .en(decoder_9_out3), .Q(register_23_q), .clk(Clk), .clr(Reset));
  Register #(.width(32)) register_24 (.D(WriteData), .en(decoder_10_out0), .Q(register_24_q), .clk(Clk), .clr(Reset));
  Register #(.width(32)) register_25 (.D(WriteData), .en(decoder_10_out1), .Q(register_25_q), .clk(Clk), .clr(Reset));
  Register #(.width(32)) register_26 (.D(WriteData), .en(decoder_10_out2), .Q(register_26_q), .clk(Clk), .clr(Reset));
  Register #(.width(32)) register_27 (.D(WriteData), .en(decoder_10_out3), .Q(register_27_q), .clk(Clk), .clr(Reset));
  Register #(.width(32)) register_28 (.D(WriteData), .en(decoder_11_out0), .Q(register_28_q), .clk(Clk), .clr(Reset));
  Register #(.width(32)) register_29 (.D(WriteData), .en(decoder_11_out1), .Q(register_29_q), .clk(Clk), .clr(Reset));
  Register #(.width(32)) register_30 (.D(WriteData), .en(decoder_11_out2), .Q(register_30_q), .clk(Clk), .clr(Reset));
  Register #(.width(32)) register_31 (.D(WriteData), .en(decoder_11_out3), .Q(register_31_q), .clk(Clk), .clr(Reset));
  // Probe on register_16_q
  // Probe on register_17_q
  // Probe on register_18_q
  // Probe on register_19_q
  // Probe on register_20_q
  // Probe on register_21_q
  // Probe on register_22_q
  // Probe on register_23_q
  // Probe on register_24_q
  // Probe on register_25_q
  // Probe on register_26_q
  // Probe on register_27_q
  // Probe on register_28_q
  // Probe on register_29_q
  // Probe on register_30_q
  // Probe on register_31_q
  Multiplexer #(.width(32), .enable("false")) multiplexer_11 (
    .in0(multiplexer_10_out), .in1(multiplexer_21_out), .out(ReadData1), .sel(ReadReg1[4]));
  Multiplexer #(.width(32), .enable("false")) multiplexer_12 (
    .in0(multiplexer_9_out), .in1(multiplexer_22_out), .out(ReadData2), .sel(ReadReg2[4]));
  Multiplexer #(.select(2), .width(32), .enable("false")) multiplexer_13 (
    .in0(register_16_q), .in1(register_17_q), .in2(register_18_q), .in3(register_19_q),
    .out(multiplexer_13_out), .sel(ReadReg1[1:0]));
  Multiplexer #(.select(2), .width(32), .enable("false")) multiplexer_14 (
    .in0(register_20_q), .in1(register_21_q), .in2(register_22_q), .in3(register_23_q),
    .out(multiplexer_14_out), .sel(ReadReg1[1:0]));
  Multiplexer #(.select(2), .width(32), .enable("false")) multiplexer_15 (
    .in0(register_24_q), .in1(register_25_q), .in2(register_26_q), .in3(register_27_q),
    .out(multiplexer_15_out), .sel(ReadReg1[1:0]));
  Multiplexer #(.select(2), .width(32), .enable("false")) multiplexer_16 (
    .in0(register_28_q), .in1(register_29_q), .in2(register_30_q), .in3(register_31_q),
    .out(multiplexer_16_out), .sel(ReadReg1[1:0]));
  Multiplexer #(.select(2), .width(32), .enable("false")) multiplexer_17 (
    .in0(register_16_q), .in1(register_17_q), .in2(register_18_q), .in3(register_19_q),
    .out(multiplexer_17_out), .sel(ReadReg2[1:0]));
  Multiplexer #(.select(2), .width(32), .enable("false")) multiplexer_18 (
    .in0(register_20_q), .in1(register_21_q), .in2(register_22_q), .in3(register_23_q),
    .out(multiplexer_18_out), .sel(ReadReg2[1:0]));
  Multiplexer #(.select(2), .width(32), .enable("false")) multiplexer_19 (
    .in0(register_24_q), .in1(register_25_q), .in2(register_26_q), .in3(register_27_q),
    .out(multiplexer_19_out), .sel(ReadReg2[1:0]));
  Multiplexer #(.select(2), .width(32), .enable("false")) multiplexer_20 (
    .in0(register_28_q), .in1(register_29_q), .in2(register_30_q), .in3(register_31_q),
    .out(multiplexer_20_out), .sel(ReadReg2[1:0]));
  Multiplexer #(.select(2), .width(32), .enable("false")) multiplexer_21 (
    .in0(multiplexer_17_out), .in1(multiplexer_18_out), .in2(multiplexer_19_out), .in3(multiplexer_20_out),
    .out(multiplexer_21_out), .sel(ReadReg2[3:2]));
  Multiplexer #(.select(2), .width(32), .enable("false")) multiplexer_22 (
    .in0(multiplexer_13_out), .in1(multiplexer_14_out), .in2(multiplexer_15_out), .in3(multiplexer_16_out),
    .out(multiplexer_22_out), .sel(ReadReg1[3:2]));
endmodule

module Testes (
  input  [5:0] Function,
  input  [1:0] ALUOp,
  output [3:0] Operation
);

  wire and_1_out, and_2_out, and_3_out, and_4_out, and_5_out, and_6_out, and_7_out, not_1_out, not_2_out,
       not_3_out, not_4_out, not_5_out, not_6_out, not_7_out, not_8_out, not_9_out, not_10_out, not_11_out,
       not_12_out, not_13_out, not_14_out, not_15_out, not_16_out, not_17_out, not_18_out, not_19_out,
       not_20_out, not_21_out, not_22_out, not_23_out, not_24_out, not_25_out, or_1_out, or_2_out,
       reg_if_id_1_p1, reg_if_id_1_p2, reg_if_id_1_p4, reg_if_id_1_p6;
  wire [1:0] reg_if_id_1_p7;
  wire [2:0] priority_encoder_1_out;
  wire [31:0] reg_if_id_1_p8;

  // Reg_IF_ID reg_if_id_1: pin names not known; wires that end beside it: reg_if_id_1_p1, reg_if_id_1_p2, reg_if_id_1_p1, reg_if_id_1_p4, reg_if_id_1_p2, reg_if_id_1_p6, reg_if_id_1_p7, reg_if_id_1_p8, reg_if_id_1_p6
  not not_1 (not_1_out, ALUOp[1]);
  and and_1 (and_1_out, not_1_out, not_2_out);
  not not_2 (not_2_out, ALUOp[0]);
  not not_3 (not_3_out, ALUOp[0]);
  not not_4 (not_4_out, Function[3]);
  and and_2 (and_2_out, ALUOp[1], not_3_out, not_4_out, not_5_out, not_6_out, not_7_out);
  not not_5 (not_5_out, Function[2]);
  not not_6 (not_6_out, Function[1]);
  not not_7 (not_7_out, Function[0]);
  not not_8 (not_8_out, ALUOp[1]);
  and and_3 (and_3_out, not_8_out, ALUOp[0]);
  not not_9 (not_9_out, ALUOp[0]);
  not not_10 (not_10_out, Function[3]);
  and and_4 (and_4_out, ALUOp[1], not_9_out, not_10_out, not_11_out, Function[1], not_12_out);
  not not_11 (not_11_out, Function[2]);
  not not_12 (not_12_out, Function[0]);
  not not_13 (not_13_out, ALUOp[0]);
  not not_14 (not_14_out, Function[4]);
  and and_5 (and_5_out, ALUOp[1], not_13_out, Function[5], not_14_out, not_15_out, Function[2], not_16_out, not_17_out);
  not not_15 (not_15_out, Function[3]);
  not not_16 (not_16_out, Function[1]);
  not not_17 (not_17_out, Function[0]);
  not not_18 (not_18_out, ALUOp[0]);
  not not_19 (not_19_out, Function[4]);
  and and_6 (and_6_out, ALUOp[1], not_18_out, Function[5], not_19_out, not_20_out, Function[2], not_21_out, Function[0]);
  not not_20 (not_20_out, Function[3]);
  not not_21 (not_21_out, Function[1]);
  not not_22 (not_22_out, ALUOp[0]);
  not not_23 (not_23_out, Function[4]);
  and and_7 (and_7_out, ALUOp[1], not_22_out, Function[5], not_23_out, Function[3], not_24_out, Function[1], not_25_out);
  not not_24 (not_24_out, Function[2]);
  not not_25 (not_25_out, Function[0]);
  control control_1 (.in_1(reg_if_id_1_p8[31:26]));  // open: RegDst, ALUSrc, MemtoReg, RegWrite, MemRead, MemWrite, Beq, Bne, Jump, Control, ALUOp
  or or_1 (or_1_out, and_1_out, and_2_out);
  or or_2 (or_2_out, and_3_out, and_4_out);
  Priority_Encoder priority_encoder_1 (
    .in0(and_5_out), .in1(and_6_out), .in2(or_1_out), .in3(or_2_out), .in4(and_7_out),
    .out(priority_encoder_1_out));  // open: in5, in6, in7, en_in, gs, en_out
  ID_EX id_ex_1 (.Control(reg_if_id_1_p7));  // open: data1__rs, data2__rt_rd, immediate, instrucao__20_16, instrucao__15_11, clock, data1__rs_2, data2__rt_rd_2, immediate_2, instrucao__20_16_2, instrucao__15_11_2, clear, pc_4, pc_4_2, RegDst_2, ALUSrc_2, MemtoReg_2, RegWrite_2, MemRead_2, MemWrite_2, Beq_2, Bne_2, Jump_2, Control_2, ALUOp_2, RegDst, ALUSrc, MemtoReg, RegWrite, MemRead, MemWrite, Beq, Bne, Jump, ALUOp
  Multiplexer #(.select(3), .width(4)) multiplexer_1 (
    .in0(4'b0000), .in1(4'b0001), .in2(4'b0010), .in3(4'b0110), .in4(4'b0111), .out(Operation),
    .sel(priority_encoder_1_out));  // open: in5, in6, in7, en
  // Probe on priority_encoder_1_out

  // Notes on the sheet:
  //   Inputs
  //   instrucao
  //   pc+4
  //   clock
  //   pc+4
  //   instrucao
  //   clear
  //   B -- OR
  //   ToDo: Fill in logic from Fig 4.13
  //   Hint: Here is the logic for the first row: 
  //   A -- if (ALUOp1=0 and ALUOp0=0)
  //   D -- then output = 2 = 0010
  //   A
  //   C
  //   A
  //   C
  //   opcode
  //   C -- if (ALUOp1=1 and ALUOp0=0 and F3, F2, F1, F0 are all 0)
  //   B
  //   B
  //   True for 0010=2
  //   True for 0110=6
  //   True for 0000=0
  //   True for 0001=1
  //   True for 0111=7
  //   ALUOp
  //   00
  //   01
  //   10
  //   11
  //   We have 5 possible outputs
  //   D
  //   LIVRO - PÁGINA 439
  //   Operation
  //   0010
  //   0110
  //   0010
  //   xxxx
  //   Depending on which input is 1,
  //   one of the outputs above will be selected.
  //   00 - xxxxx - 0010
  //   01 - xxxxx - 0110
  //   10 - 100000 - 0010
  //   10 - 100010 - 0110
  //   10 - 100100 - 0000
  //   10 - 100101 - 0001
  //   10 - 101010 - 0010
endmodule

module load_store (
  input  [31:0] Entrada,
  input  [1:0] Control,
  output [31:0] Saida
);

  wire [31:0] bit_extender_1_out, bit_extender_2_out;

  // Probe on Entrada
  // Probe on Entrada
  // Probe on Entrada[7:0]
  // Probe on Entrada[15:0]
  assign bit_extender_1_out = {{24{1'b0}}, Entrada[7:0]};  // Bit_Extender bit_extender_1
  assign bit_extender_2_out = {{16{1'b0}}, Entrada[15:0]};  // Bit_Extender bit_extender_2
  // Probe on bit_extender_1_out
  // Probe on bit_extender_2_out
  Multiplexer #(.select(2), .width(32), .enable("false")) multiplexer_1 (
    .in0(bit_extender_1_out), .in1(Entrada), .in2(bit_extender_2_out), .out(Saida), .sel(Control));  // open: in3

  // Notes on the sheet:
  //   Load/Store Byte
  //   Load/Store Half
  //   Load/Store Word
endmodule

module branch (
  input  beq,
  input  bne,
  input  ZERO,
  output C
);

  wire and_1_out, and_2_out, not_1_out, not_2_out, not_3_out;

  not not_1 (not_1_out, beq);
  not not_2 (not_2_out, ZERO);
  not not_3 (not_3_out, bne);
  and and_1 (and_1_out, not_1_out, bne, not_2_out);
  and and_2 (and_2_out, beq, not_3_out, ZERO);
  or or_1 (C, and_1_out, and_2_out);
endmodule

module Reg_IF_ID (
  input  [31:0] pc_4,
  input  [31:0] instruction,
  input  clock,
  input  clear,
  output [31:0] pc_4___out,
  output [31:0] instruction___out
);

  Register #(.width(32)) register_1 (.D(pc_4), .Q(pc_4___out), .clk(clock), .clr(clear));  // open: en
  Register #(.width(32)) register_2 (.D(instruction), .Q(instruction___out), .clk(clock), .clr(clear));  // open: en
endmodule

module ID_EX (
  input  RegDst,
  input  ALUSrc,
  input  [31:0] pc_4,
  input  MemtoReg,
  input  RegWrite,
  input  [31:0] data1__rs,
  input  MemRead,
  input  [31:0] data2__rt_rd,
  input  MemWrite,
  input  Beq,
  input  [31:0] immediate,
  input  Bne,
  input  [4:0] instrucao__20_16,
  input  Jump,
  input  [4:0] instrucao__15_11,
  input  [1:0] Control,
  input  [1:0] ALUOp,
  input  clock,
  input  clear,
  output RegDst_2,
  output ALUSrc_2,
  output [31:0] pc_4_2,
  output MemtoReg_2,
  output RegWrite_2,
  output [31:0] data1__rs_2,
  output MemRead_2,
  output [31:0] data2__rt_rd_2,
  output MemWrite_2,
  output Beq_2,
  output [31:0] immediate_2,
  output Bne_2,
  output [4:0] instrucao__20_16_2,
  output Jump_2,
  output [4:0] instrucao__15_11_2,
  output [1:0] Control_2,
  output [1:0] ALUOp_2
);

  Register #(.width(1)) register_1 (.D(RegDst), .Q(RegDst_2), .clk(clock), .clr(clear));  // open: en
  Register #(.width(1)) register_2 (.D(ALUSrc), .Q(ALUSrc_2), .clk(clock), .clr(clear));  // open: en
  Register #(.width(1)) register_3 (.D(MemtoReg), .Q(MemtoReg_2), .clk(clock), .clr(clear));  // open: en
  Register #(.width(1)) register_4 (.D(RegWrite), .Q(RegWrite_2), .clk(clock), .clr(clear));  // open: en
  Register #(.width(1)) register_5 (.D(MemRead), .en(MemRead), .Q(MemRead_2), .clk(clock), .clr(clear));
  Register #(.width(1)) register_6 (.D(MemWrite), .Q(MemWrite_2), .clk(clock), .clr(clear));  // open: en
  Register #(.width(1)) register_7 (.D(Beq), .Q(Beq_2), .clk(clock), .clr(clear));  // open: en
  Register #(.width(1)) register_8 (.D(Bne), .Q(Bne_2), .clk(clock), .clr(clear));  // open: en
  Register #(.width(1)) register_9 (.D(Jump), .Q(Jump_2), .clk(clock), .clr(clear));  // open: en
  Register #(.width(2)) register_10 (.D(Control), .Q(Control_2), .clk(clock), .clr(clear));  // open: en
  Register #(.width(2)) register_11 (.D(ALUOp), .Q(ALUOp_2), .clk(clock), .clr(clear));  // open: en
  Register #(.width(32)) register_12 (.D(pc_4), .Q(pc_4_2), .clk(clock), .clr(clear));  // open: en
  Register #(.width(32)) register_13 (.D(data1__rs), .Q(data1__rs_2), .clk(clock), .clr(clear));  // open: en
  Register #(.width(32)) register_14 (.D(data2__rt_rd), .Q(data2__rt_rd_2), .clk(clock), .clr(clear));  // open: en
  Register #(.width(32)) register_15 (.D(immediate), .Q(immediate_2), .clk(clock), .clr(clear));  // open: en
  Register #(.width(5)) register_16 (
    .D(instrucao__20_16), .Q(instrucao__20_16_2), .clk(clock), .clr(clear));  // open: en
  Register #(.width(5)) register_17 (
    .D(instrucao__15_11), .Q(instrucao__15_11_2), .clk(clock), .clr(clear));  // open: en
endmodule

module EX_MEM (
  input  MemToReg,
  input  [31:0] pc_deslocado,
  input  WriteReg,
  input  zero,
  input  Load,
  input  [31:0] AluResult,
  input  store,
  input  beq,
  input  [31:0] rt,
  input  bne,
  input  [4:0] WriteReg_2,
  input  jump,
  input  [1:0] control,
  input  clock,
  input  clear,
  output out_16,
  output [31:0] out_17,
  output out_18,
  output out_19,
  output out_20,
  output [31:0] out_21,
  output out_22,
  output out_23,
  output [31:0] out_24,
  output out_25,
  output [4:0] out_26,
  output out_27,
  output [1:0] out_28
);

  Register #(.width(32)) register_1 (.D(pc_deslocado), .Q(out_17), .clk(clock), .clr(clear));  // open: en
  Register #(.width(1)) register_2 (.D(zero), .Q(out_19), .clk(clock), .clr(clear));  // open: en
  Register #(.width(32)) register_3 (.D(AluResult), .Q(out_21), .clk(clock), .clr(clear));  // open: en
  Register #(.width(32)) register_4 (.D(rt), .Q(out_24), .clk(clock), .clr(clear));  // open: en
  Register #(.width(5)) register_5 (.D(WriteReg_2), .Q(out_26), .clk(clock), .clr(clear));  // open: en
  Register #(.width(1)) register_6 (.D(MemToReg), .Q(out_16), .clk(clock), .clr(clear));  // open: en
  Register #(.width(1)) register_7 (.D(WriteReg), .Q(out_18), .clk(clock), .clr(clear));  // open: en
  Register #(.width(1)) register_8 (.D(Load), .Q(out_20), .clk(clock), .clr(clear));  // open: en
  Register #(.width(1)) register_9 (.D(store), .Q(out_22), .clk(clock), .clr(clear));  // open: en
  Register #(.width(1)) register_10 (.D(beq), .Q(out_23), .clk(clock), .clr(clear));  // open: en
  Register #(.width(1)) register_11 (.D(bne), .Q(out_25), .clk(clock), .clr(clear));  // open: en
  Register #(.width(1)) register_12 (.D(jump), .Q(out_27), .clk(clock), .clr(clear));  // open: en
  Register #(.width(2)) register_13 (.D(control), .Q(out_28), .clk(clock), .clr(clear));  // open: en
endmodule

module MEM_WB (
  input  [31:0] pc_deslocado,
  input  [31:0] AluResult,
  input  MemToReg,
  input  WriteReg,
  input  [4:0] RegWrite,
  input  clock,
  input  clear,
  output [31:0] out_8,
  output [31:0] out_9,
  output out_10,
  output out_11,
  output [4:0] out_12
);

  Register #(.width(32)) register_1 (.D(pc_deslocado), .Q(out_8), .clk(clock), .clr(clear));  // open: en
  Register #(.width(32)) register_2 (.D(AluResult), .Q(out_9), .clk(clock), .clr(clear));  // open: en
  Register #(.width(1)) register_3 (.D(MemToReg), .Q(out_10), .clk(clock), .clr(clear));  // open: en
  Register #(.width(1)) register_4 (.D(WriteReg), .Q(out_11), .clk(clock), .clr(clear));  // open: en
  Register #(.width(5)) register_5 (.D(RegWrite), .Q(out_12), .clk(clock), .clr(clear));  // open: en
endmodule
